# Fritzing sketch DeviceWheel-circuit (saved by Fritzing 0.9.3b)

parts:
  Part1 = Adafruit HUZZAH32 ESP32 Feather [part_number="Adafruit #3405"]
  R1 = Resistor [tolerance=±5% resistance=1k package="2010 [SMD]"]
  LED1 = LED - 3mm [color="Blue (430nm)" package="3 mm [THT]"]
  S3 = Toggle Switch [package=THT]

nets:
  GND: Part1.GND, LED1.cathode, S3.L1
  N1: Part1.EN, S3.COM
  N2: Part1.IO12_A11, R1.Pin_1
  N3: R1.Pin_0, LED1.anode
